# Fritzing sketch esp32 (saved by Fritzing 0.9.3b)
breadboards: 1

parts:
  U1 = ESP32S-HiLetgo [part_number=ESP32S-HiLetgo]
  BAT1 = BC9VPC [package=bc9vpc]
  Part1 = Soil Moisture Sensor

nets:
  VIN: U1.VIN, U1.GPIO6, BAT1.V+, Part1.VCC
  N1: U1.GPIO19, Part1.SIG
  N2: BAT1.V-, Part1.GND

custom parts:
  ESP32S-HiLetgo: HiLetgo ESP-WROOM-32 ESP32 ESP-32S Development Board 2.4GHz Dual-Mode WiFi + Bluetooth Dual Cores Microcontroller The ESP32 integrated with Antenna switches, RF Balun, power amplifiers, low-noise amplifiers, filters, and management modules, and the entire solution occupies the least area of PCB. 2.4 GHz Wi-Fi plus Bluetooth dual-mode chip, with TSMC Ultra-low power consumption 40nm technology,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
